# Fritzing sketch led_cloud (saved by Fritzing 0.9.3b)
circuit board: 6.2559cm x 4.12673cm
breadboards: 1

parts:
  TRINKET_3V = mystery part, 10 pins [chip_label="Trinket 3V"]
  R1 = Resistor [tolerance=±5% resistance=470 package=THT]
  R3 = Resistor [tolerance=±5% resistance=560 package=THT]
  RGB_LED = RGB LED - (4 legs) [package="5 mm [THT]"]
  FET_N = Basic FET N-Channel [part_number=IRLB8721 package="TO220 [THT]"]
  R2 = Resistor [tolerance=±5% resistance=470 package=THT]
  FET_N_2 = Basic FET N-Channel [part_number=IRLB8721 package="TO220 [THT]"]
  FET_N_3 = Basic FET N-Channel [part_number=IRLB8721 package="TO220 [THT]"]
  V1 = DC Power [voltage=12V]
  +12V = Header 1 [package=1x01_offset]
  RED = Header 1 [package=1x01_offset]
  GREEN = Header 1 [package=1x01_offset]
  BLUE = Header 1 [package=1x01_offset]

nets:
  N1: TRINKET_3V.pin1, RGB_LED.common_anode, V1.V+, +12V.1
  N2: TRINKET_3V.pin2, FET_N.source, FET_N_2.source, FET_N_3.source, V1.V-
  N3: TRINKET_3V.pin3, FET_N_3.gate
  N4: TRINKET_3V.pin8, FET_N_2.gate
  N5: TRINKET_3V.pin9, FET_N.gate
  N6: R1.Pin_0, RGB_LED.blue_cathode
  N7: R1.Pin_1, FET_N.drain, BLUE.1
  N8: R3.Pin_0, RGB_LED.red_cathode
  N9: R3.Pin_1, FET_N_3.drain, RED.1
  N10: RGB_LED.green_cathode, R2.Pin_0
  N11: R2.Pin_1, FET_N_2.drain, GREEN.1
